// Digital circuit CORE.dig as structural Verilog
module CORE (
  input  clk,
  input  RST,
  input  CLR
);

  wire ALUD_CO, ALUDH_OE, ALUDL_OE, ALUS_OE, and_3_out, and_4_out, and_5_out, and_6_out, ASSERT_p5, BR_Q,
       button_1_out, CLK_t, CLKR, comparator_1_eq, comparator_1_gt, comparator_1_lt, comparator_2_eq,
       comparator_3_eq, DC_JUMP, EXR_q, GO, IMMED_OE, IRQ_OE, not_1_out, not_2_out, RAM_OE, RAM_WE, RF_HWE,
       RF_LWE, RF_SFR, RFSRCR_WE, ROM_OE, SFR_OE, SR_WE, WR_WE, XRAM_OE;
  wire [2:0] BR_SRC, BUS_SRC, JUMP_TYPE;
  wire [3:0] ALUSD_FUNC, multiplexer_2_out, RF_SRC;
  wire [5:4] multiplexer_2_out_2;
  wire [6:0] and_2_out;
  wire [7:0] DBUS, ECR_q, IMMED, RF_Q, SR_q, WR_q;
  wire [7:4] RFSRCR_q;
  wire [11:0] ADDRESS, dcouter_1_q;
  wire [47:44] DECODER_2_d;

  Decoder #(.Selector_Bits(3)) decoder_1 (
    .sel(BUS_SRC), .out_0(ALUS_OE), .out_1(ALUDL_OE), .out_2(ALUDH_OE), .out_3(IMMED_OE), .out_4(RAM_OE),
    .out_5(XRAM_OE), .out_6(ROM_OE), .out_7(IRQ_OE));
  DCOUTER #(.generic("Bits := 12;")) dcouter_1 (
    .CLK(CLK_t), .CLR(CLR), .CNT(1'b1), .LE(DC_JUMP), .D(ADDRESS), .Q(dcouter_1_q));
  Comparator #(.Bits(8)) comparator_1 (
    .a(RF_Q), .b(IMMED), .gt(comparator_1_gt), .eq(comparator_1_eq), .lt(comparator_1_lt));
  // Probe on dcouter_1_q
  Multiplexer #(.Selector_Bits(3)) multiplexer_1 (
    .sel(JUMP_TYPE), .in_0(1'b0), .in_1(1'b1), .in_2(comparator_1_gt), .in_3(comparator_1_eq),
    .in_4(comparator_1_lt), .in_5(BR_Q), .in_6(RST), .in_7(1'b0), .out(DC_JUMP));
  ROM #(.AddrBits(12), .Bits(48)) DECODER_2 (
    .A(dcouter_1_q), .sel(1'b1),
    .D({DECODER_2_d, IMMED, ADDRESS, JUMP_TYPE, ALUSD_FUNC, RAM_WE, RFSRCR_WE, BR_SRC, SR_WE, WR_WE, BUS_SRC, RF_SFR, RF_HWE, RF_LWE, RF_SRC}));
  Register #(.Bits(8)) RFSRCR (.D(DBUS), .C(CLK_t), .en(RFSRCR_WE), .Q({RFSRCR_q, and_2_out[3:0]}));
  and and_1 (and_2_out[5], RFSRCR_q[4], RAM_WE);
  and and_2 (and_2_out[6], RFSRCR_q[4], RAM_OE);
  Multiplexer #(.Bits(7)) multiplexer_2 (
    .sel(RF_SFR), .in_0({1'b0, RF_HWE, RF_LWE, RF_SRC}),
    .in_1({and_2_out[6:5], and_2_out[5], and_2_out[3:0]}),
    .out({SFR_OE, multiplexer_2_out_2, multiplexer_2_out}));
  // Probe on RF_SRC
  // Probe on RF_LWE
  // Probe on RF_HWE
  // Probe on RF_SFR
  // Probe on BUS_SRC
  // Probe on WR_WE
  // Probe on SR_WE
  // Probe on BR_SRC
  // Probe on RFSRCR_WE
  // Probe on RAM_WE
  // Probe on ALUSD_FUNC
  // Probe on JUMP_TYPE
  // Probe on ADDRESS
  // Probe on IMMED
  Button button_1 (.out(button_1_out));
  Button button_2 (.out(GO));
  PullDown #(.Bits(8)) pulldown_1 (.out(DBUS));
  // reg_file RF: pin names not known; wires that end beside it: CLK_t, multiplexer_2_out, DBUS, multiplexer_2_out_2[4], multiplexer_2_out_2[5], RF_Q
  BR BR (.CLK(CLK_t), .nCLR(CLR), .S(BR_SRC), .I4(ALUD_CO), .I5(ALUD_CO), .I7(RF_Q[0]), .I6(RF_Q[7]), .Q(BR_Q));
  // SwitchDT switchdt_1: pin names not known; wires that end beside it: clk, button_1_out, CLKR
  // Probe on DBUS
  // Probe on RF_Q
  reg__sync_clear #(.generic("Bits := 8;")) WR (.D(DBUS), .CLK(CLK_t), .CLR(CLR), .LE(WR_WE), .Q(WR_q));
  reg__sync_clear #(.generic("Bits := 8;")) SR (.D(DBUS), .CLK(CLK_t), .CLR(CLR), .LE(SR_WE), .Q(SR_q));
  and and_3 (and_3_out, CLK_t, not_1_out);
  not not_1 (not_1_out, CLK_t);
  assign DBUS = SFR_OE ? RF_Q : 8'bz;  // Driver driver_1
  // Probe on WR_q
  // Probe on SR_q
  and and_4 (and_4_out, RAM_WE, and_3_out);
  ALU ALU (
    .A(RF_Q), .B(WR_q), .S(ALUSD_FUNC), .CI(BR_Q), .SOE(ALUS_OE), .DOE(ALUDL_OE), .FOE(ALUDH_OE), .O(DBUS),
    .ALUDF(ALUD_CO));
  // Probe on {SR_q, WR_q}
  ROM #(.AddrBits(16), .isProgramMemory("true"), .Bits(8)) ROM (.A({SR_q, WR_q}), .sel(ROM_OE), .D(DBUS));
  // ASSERT ASSERT: pin names not known; wires that end beside it: CLK_t, DBUS, SR_q, RAM_WE, ASSERT_p5, CLK_t
  RAMSinglePortSel #(.AddrBits(7), .isProgramMemory("true"), .Bits(8)) RAM (
    .A(SR_q[6:0]), .CS(not_2_out), .WE(and_4_out), .OE(RAM_OE), .D(DBUS));
  not not_2 (not_2_out, SR_q[7]);
  assign DBUS = IMMED_OE ? IMMED : 8'bz;  // Driver driver_2
  STALL stall_1 (.C(CLKR), .AC(ASSERT_p5), .S(GO), .OAC(CLK_t));  // open: G, nCLR, O
  Comparator #(.Bits(8)) comparator_2 (.a(SR_q), .b(8'hee), .eq(comparator_2_eq));  // open: gt, lt
  Comparator #(.Bits(8)) comparator_3 (.a(SR_q), .b(8'hef), .eq(comparator_3_eq));  // open: gt, lt
  and and_5 (and_5_out, comparator_2_eq, RAM_WE);
  and and_6 (and_6_out, comparator_3_eq, RAM_WE);
  Register EXR (.D(1'b1), .C(CLK_t), .en(and_5_out), .Q(EXR_q));
  Register #(.Bits(8)) ECR (.D(DBUS), .C(CLK_t), .en(and_6_out), .Q(ECR_q));
  // Probe on EXR_q
  // Probe on ECR_q

  // Notes on the sheet:
  //   clk: Hz: 2147483647
  //   contents of DECODER_2 (hex, n*v repeats v):
  //   12dc80488,80889,33a,580,85106,c3135,450b8,400b9,8007f80000a,c004580000a,e002680000a,
  //   f001780000a,f801180040a,a00bc,80485,1a088c,236,f401480000a,f601380000a,f501480000a,
  //   f201680000a,f301680000a,f101780000a,e801f80000a,ec01c80000a,ee01b80000a,ef01b80000a,
  //   ed01c80000a,ea01e80000a,eb01e80000a,e901f80000a,e402380000a,e602280000a,e702280000a,
  //   e502380000a,e202580000a,e302580000a,e102680000a,d003680000a,d802f80000a,dc02c80000a,
  //   de02b80000a,df02b80000a,dd02c80000a,da02e80000a,db02e80000a,d902f80000a,d403380000a,
  //   d603280000a,d703280000a,d503380000a,d203580000a,d303580000a,d103680000a,c803e80000a,
  //   cc03b80000a,ce03a80000a,cf03a80000a,cd03b80000a,ca03d80000a,cb03d80000a,c903e80000a,
  //   c404280000a,c604180000a,c704180000a,c504280000a,c204480000a,c304480000a,c104580000a,
  //   a006880000a,b005680000a,b804f80000a,bc04c80000a,be04b80000a,bf04b80000a,bd04c80000a,
  //   ba04e80000a,bb04e80000a,b904f80000a,b405380000a,b605280000a,b705280000a,b505380000a,
  //   b205580000a,b305580000a,b105680000a,a805e80000a,ac05b80000a,ae05a80000a,af05a80000a,
  //   ad05b80000a,aa05d80000a,ab05d80000a,a905e80000a,a406280000a,a606180000a,a706180000a,
  //   a506280000a,a206780000a,a306780000a,3580,450b1,1152400b2,a106880000a,9007080000a,
  //   9806a80000a,9406d80000a,9606c80000a,9506d80000a,9206f80000a,9306f80000a,9107080000a,
  //   8807880000a,8c07580000a,8e07480000a,8f07480000a,8d07580000a,8a07780000a,8b07780000a,
  //   8907880000a,8407c80000a,8607b80000a,8707b80000a,8507c80000a,8207e80000a,8307e80000a,
  //   8107f80000a,400d380000a,600b480000a,700a580000a,7808a80000a,7c08780000a,7e08680000a,
  //   7f08680000a,7d08780000a,7a08980000a,7b08980000a,7908a80000a,740a280000a,7608d80000a,
  //   7708d80000a,7509c80000a,80488,80889,33c,3580,450b8,408b9,80488,700,6800c,8088c,b00c0,
  //   3580,450b8,1152400b9,80488,80889,336,3580,450b8,1152400b9,720a480000a,730a480000a,
  //   710a580000a,680ad80000a,6c0aa80000a,6e0a980000a,6f0a980000a,6d0aa80000a,6a0ac80000a,
  //   6b0ac80000a,690ad80000a,640b180000a,660b080000a,670b080000a,650b180000a,620b380000a,
  //   630b380000a,610b480000a,500c480000a,580bd80000a,5c0ba80000a,5e0b980000a,5f0b980000a,
  //   5d0ba80000a,5a0bc80000a,5b0bc80000a,590bd80000a,540c180000a,560c080000a,570c080000a,
  //   550c180000a,520c380000a,530c380000a,510c480000a,480cc80000a,4c0c980000a,4e0c880000a,
  //   4f0c880000a,4d0c980000a,4a0cb80000a,4b0cb80000a,490cc80000a,440d080000a,460cf80000a,
  //   470cf80000a,450d080000a,420d280000a,430d280000a,410d380000a,200f380000a,300e480000a,
  //   380dd80000a,3c0da80000a,3e0d980000a,3f0d980000a,3d0da80000a,3a0dc80000a,3b0dc80000a,
  //   390dd80000a,340e180000a,360e080000a,370e080000a,350e180000a,320e380000a,330e380000a,
  //   310e480000a,280ec80000a,2c0e980000a,2e0e880000a,2f0e880000a,2d0e980000a,2a0eb80000a,
  //   2b0eb80000a,290ec80000a,240f080000a,260ef80000a,270ef80000a,250f080000a,220f280000a,
  //   230f280000a,210f380000a,1010380000a,180fc80000a,1c0f980000a,1e0f880000a,1f0f880000a,
  //   1d0f980000a,1a0fb80000a,1b0fb80000a,190fc80000a,1410080000a,160ff80000a,170ff80000a,
  //   1510080000a,1210280000a,1310280000a,1110380000a,810b80000a,c10880000a,e10780000a,
  //   f10780000a,d10880000a,a10a80000a,b10a80000a,910b80000a,411080000a,610e80000a,710e80000a,
  //   510f80000a,100036,211380000a,311380000a,80036,111580000a,115200000,80000880483,3bc,
  //   e04bc,100080000c,80484,1600bc,8048b,a00bd,a00be,80484,16348d,6508c,a00000,10048c,
  //   e00be,40000e,c00bb,100830,90088,100830,90089,2043c,1b9,2a00b8,1b6,1b7,1b0,1b5,1b1,
  //   1b2,1b3,1b4,1b8,1b9,1ba,12dc001bb,200000
  //   contents of ROM (hex, n*v repeats v):
  //   75,ff,0,75,fe,0,75,fd,1,75,ff,0,75,fe,0,75,fd,2,75,ff,0,75,fe,0,75,fd,3,75,ff,2,75,
  //   fe,40,75,fd,1,75,ff,2,75,fe,40,75,fd,2,75,ff,2,75,fe,40,75,fd,3,75,ff,de,75,fe,a0,
  //   75,fd,1,75,ff,de,75,fe,a0,75,fd,2,75,ff,de,75,fe,a0,75,fd,3,75,ef,0,75,ee,1
endmodule
